// Logisim project LucasMartini.circ as structural Verilog
module main (
  input  s,
  input  in_2,
  input  e,
  input  set0,
  input  set1,
  input  set2,
  input  set3,
  input  in_8,
  input  clock,
  input  enable0,
  input  enable1,
  input  enable2,
  input  enable3,
  input  in_14,
  input  in_15,
  input  [2:0] op,
  input  in_17,
  input  in_18,
  input  enable_acumulador,
  input  set_acumulador,
  output [7:0] out_21,
  output out_22,
  output out_23,
  output out_24,
  output out_25
);

  wire ula_1_a_igual, ula_1_a_maior, ula_1_c_out, ula_1_igual_0, undriven;
  wire [7:0] b1_out_3, controlled_buffer_1_out, IAR_q, IR_q, MAR_q, register_1_q, register_2_q, register_3_q,
       register_4_q, register_5_q, TMP_q, ula_1_saida;

  Register TMP (.D(controlled_buffer_1_out), .Q(TMP_q), .clk(in_8));  // open: en, clr
  bus_1 b1 (.in_1(TMP_q), .out_3(b1_out_3), .in_2(in_14));
  ULA ula_1 (
    .in_2(controlled_buffer_1_out), .in_3(b1_out_3), .saida(ula_1_saida), .in_1(op), .c_out(ula_1_c_out),
    .a_maior(ula_1_a_maior), .a_igual(ula_1_a_igual), .igual_0(ula_1_igual_0));
  Register register_1 (.D(ula_1_saida), .Q(register_1_q), .clk(set_acumulador));  // open: en, clr
  assign controlled_buffer_1_out = enable_acumulador ? register_1_q : 8'bz;  // Controlled_Buffer controlled_buffer_1
  flag flags (
    .in_1(ula_1_c_out), .in_2(ula_1_a_maior), .in_3(ula_1_a_igual), .in_4(ula_1_igual_0), .in_5(in_17),
    .out_6(out_22), .out_7(out_23), .out_8(out_24), .out_9(out_25));
  assign controlled_buffer_1_out = enable0 ? register_2_q : 8'bz;  // Controlled_Buffer controlled_buffer_2
  Register register_2 (.D(controlled_buffer_1_out), .Q(register_2_q), .clk(set0));  // open: en, clr
  // Probe on controlled_buffer_1_out
  assign controlled_buffer_1_out = enable1 ? register_3_q : 8'bz;  // Controlled_Buffer controlled_buffer_3
  Register register_3 (.D(controlled_buffer_1_out), .Q(register_3_q), .clk(set1));  // open: en, clr
  assign controlled_buffer_1_out = enable2 ? register_4_q : 8'bz;  // Controlled_Buffer controlled_buffer_4
  Register register_4 (.D(controlled_buffer_1_out), .Q(register_4_q), .clk(set2));  // open: en, clr
  Register IAR (.D(controlled_buffer_1_out), .Q(IAR_q), .clk(undriven));  // open: en, clr
  assign controlled_buffer_1_out = in_18 ? IAR_q : 8'bz;  // Controlled_Buffer controlled_buffer_5
  assign controlled_buffer_1_out = enable3 ? register_5_q : 8'bz;  // Controlled_Buffer controlled_buffer_6
  Register register_5 (.D(controlled_buffer_1_out), .Q(register_5_q), .clk(set3));  // open: en, clr
  Register IR (.D(controlled_buffer_1_out), .Q(IR_q));  // open: en, clk, clr
  Register MAR (.D(controlled_buffer_1_out), .Q(MAR_q), .clk(in_2));  // open: en, clr
  RAM ram_1 (.addr(MAR_q), .we(s), .oe(e), .clk(clock), .din(controlled_buffer_1_out), .dout(out_21));
  assign controlled_buffer_1_out = in_15 ? out_21 : 8'bz;  // Controlled_Buffer controlled_buffer_7
endmodule

module Somador1Bit (
  input  c,
  input  a,
  input  b,
  output out1,
  output out2
);

  wire and_1_out, and_2_out, and_3_out, xor_1_out;

  xor xor_1 (xor_1_out, a, b);
  and and_1 (and_1_out, a, c);
  and and_2 (and_2_out, a, b);
  and and_3 (and_3_out, b, c);
  xor xor_2 (out1, xor_1_out, c);
  or or_1 (out2, and_1_out, and_2_out, and_3_out);
endmodule

module Somador8Bits (
  input  in_1,
  input  [7:0] in_2,
  input  [7:0] in_3,
  output [7:0] out_4,
  output out_5
);

  wire somador1bit_1_out2, somador1bit_2_out2, somador1bit_3_out2, somador1bit_4_out2, somador1bit_5_out2,
       somador1bit_6_out2, somador1bit_7_out2;

  Somador1Bit somador1bit_1 (.a(in_2[0]), .b(in_3[0]), .c(in_1), .out2(somador1bit_1_out2), .out1(out_4[0]));
  Somador1Bit somador1bit_2 (
    .a(in_2[1]), .b(in_3[1]), .c(somador1bit_1_out2), .out2(somador1bit_2_out2), .out1(out_4[1]));
  Somador1Bit somador1bit_3 (
    .a(in_2[2]), .b(in_3[2]), .c(somador1bit_2_out2), .out2(somador1bit_3_out2), .out1(out_4[2]));
  Somador1Bit somador1bit_4 (
    .a(in_2[3]), .b(in_3[3]), .c(somador1bit_3_out2), .out2(somador1bit_4_out2), .out1(out_4[3]));
  Somador1Bit somador1bit_5 (
    .a(in_2[4]), .b(in_3[4]), .c(somador1bit_4_out2), .out2(somador1bit_5_out2), .out1(out_4[4]));
  Somador1Bit somador1bit_6 (
    .a(in_2[5]), .b(in_3[5]), .c(somador1bit_5_out2), .out2(somador1bit_6_out2), .out1(out_4[5]));
  Somador1Bit somador1bit_7 (
    .a(in_2[6]), .b(in_3[6]), .c(somador1bit_6_out2), .out2(somador1bit_7_out2), .out1(out_4[6]));
  Somador1Bit somador1bit_8 (.a(in_2[7]), .b(in_3[7]), .c(somador1bit_7_out2), .out2(out_5), .out1(out_4[7]));
endmodule

module Memoria1Bit (
  input  in_1,
  input  in_2,
  output out_3
);

  wire nand_1_out, nand_2_out, nand_4_out;

  nand nand_1 (nand_1_out, in_1, in_2);
  // Probe on nand_1_out
  nand nand_2 (nand_2_out, nand_1_out, in_2);
  nand nand_3 (out_3, nand_1_out, nand_4_out);
  nand nand_4 (nand_4_out, out_3, nand_2_out);
endmodule

module Registrador (
  input  [7:0] Input8Bit,
  input  set,
  input  enable,
  output [7:0] Output8BI
);

  wire memoria1bit_1_out_3, memoria1bit_2_out_3, memoria1bit_3_out_3, memoria1bit_4_out_3,
       memoria1bit_5_out_3, memoria1bit_6_out_3, memoria1bit_7_out_3, memoria1bit_8_out_3;

  Memoria1Bit memoria1bit_1 (.in_1(Input8Bit[0]), .in_2(set), .out_3(memoria1bit_1_out_3));
  Memoria1Bit memoria1bit_2 (.in_1(Input8Bit[1]), .in_2(set), .out_3(memoria1bit_2_out_3));
  Memoria1Bit memoria1bit_3 (.in_1(Input8Bit[2]), .in_2(set), .out_3(memoria1bit_3_out_3));
  Memoria1Bit memoria1bit_4 (.in_1(Input8Bit[3]), .in_2(set), .out_3(memoria1bit_4_out_3));
  Memoria1Bit memoria1bit_5 (.in_1(Input8Bit[4]), .in_2(set), .out_3(memoria1bit_5_out_3));
  Memoria1Bit memoria1bit_6 (.in_1(Input8Bit[5]), .in_2(set), .out_3(memoria1bit_6_out_3));
  Memoria1Bit memoria1bit_7 (.in_1(Input8Bit[6]), .in_2(set), .out_3(memoria1bit_7_out_3));
  Memoria1Bit memoria1bit_8 (.in_1(Input8Bit[7]), .in_2(set), .out_3(memoria1bit_8_out_3));
  and and_1 (Output8BI[0], memoria1bit_1_out_3, enable);
  and and_2 (Output8BI[1], memoria1bit_2_out_3, enable);
  and and_3 (Output8BI[2], memoria1bit_3_out_3, enable);
  and and_4 (Output8BI[3], memoria1bit_4_out_3, enable);
  and and_5 (Output8BI[4], memoria1bit_5_out_3, enable);
  and and_6 (Output8BI[5], memoria1bit_6_out_3, enable);
  and and_7 (Output8BI[6], memoria1bit_7_out_3, enable);
  and and_8 (Output8BI[7], memoria1bit_8_out_3, enable);
endmodule

module ShiftRight (
  input  in_1,
  input  [7:0] in_2,
  output [7:0] out_3,
  output out_4
);


  assign out_3 = {in_1, in_2[7:1]};
  assign out_4 = in_2[0];
endmodule

module ShiftLeft (
  input  in_1,
  input  [7:0] in_2,
  output [7:0] out_3,
  output out_4
);


  assign out_3 = {in_2[6:0], in_1};
  assign out_4 = in_2[7];
endmodule

module ULA (
  input  [2:0] in_1,
  input  [7:0] in_2,
  input  [7:0] in_3,
  output c_out,
  output [7:0] saida,
  output a_maior,
  output a_igual,
  output igual_0
);

  wire adder_1_cout, or_2_out, shiftleft_1_out_4, shiftright_1_out_4;
  wire [7:0] adder_1_out, and_1_out, not_1_out, or_1_out, shiftleft_1_out_3, shiftright_1_out_3, xor_1_out;

  Comparator comparator_1 (.a(in_2), .b(in_3), .gt(a_maior), .eq(a_igual));  // open: lt
  Adder adder_1 (.a(in_2), .b(in_3), .out(adder_1_out), .cin(1'b0), .cout(adder_1_cout));
  ShiftRight shiftright_1 (.in_2(in_2), .in_1(1'b0), .out_4(shiftright_1_out_4), .out_3(shiftright_1_out_3));
  ShiftLeft shiftleft_1 (.in_2(in_2), .in_1(1'b0), .out_4(shiftleft_1_out_4), .out_3(shiftleft_1_out_3));
  assign not_1_out = ~in_2;  // NOT_Gate not_1, 8 bits wide
  assign and_1_out = in_2 & in_3;  // AND_Gate and_1, 8 bits wide
  assign or_1_out = in_2 | in_3;  // OR_Gate or_1, 8 bits wide
  assign xor_1_out = in_2 ^ in_3;  // XOR_Gate xor_1, 8 bits wide
  Multiplexer #(.select(3), .width(8)) multiplexer_1 (
    .in0(adder_1_out), .in1(shiftright_1_out_3), .in2(shiftleft_1_out_3), .in3(not_1_out), .in4(and_1_out),
    .in5(or_1_out), .in6(xor_1_out), .in7(in_2), .out(saida), .sel(in_1));
  or or_2 (or_2_out, saida[0], saida[1], saida[2], saida[3], saida[4], saida[5], saida[6], saida[7]);
  Multiplexer #(.select(3)) multiplexer_2 (
    .in0(adder_1_cout), .in1(shiftright_1_out_4), .in2(shiftleft_1_out_4), .in3(1'b0), .in4(1'b0),
    .in5(1'b0), .in6(1'b0), .in7(1'b0), .out(c_out), .sel(in_1));
  not not_2 (igual_0, or_2_out);
endmodule

module Clk (
  output clk_s,
  output main,
  output clk_e
);

  wire clk_d_out;

  Clock #(.highDuration(2), .lowDuration(2)) clock_1 (.out(main));
  Clock #(.highDuration(2), .lowDuration(2), .phaseOffset(3)) clk_d (.out(clk_d_out));
  and and_1 (clk_s, clk_d_out, main);
  or or_1 (clk_e, main, clk_d_out);
endmodule

module Stepper (
  input  in_1,
  output out_2,
  output step1,
  output step6,
  output step2,
  output step5,
  output step3,
  output step4
);

  wire decoder_1_out7;
  wire [2:0] counter_1_q;

  Counter #(.max('h7), .width(3)) counter_1 (
    .D(counter_1_q), .Q(counter_1_q), .clk(in_1), .clr(decoder_1_out7));  // open: load, count, carry, up
  Decoder #(.enable("false"), .select(3)) decoder_1 (
    .out0(out_2), .out1(step1), .out2(step2), .out3(step3), .out4(step4), .out5(step5), .out6(step6),
    .out7(decoder_1_out7), .sel(counter_1_q));
endmodule

module UC (
  input  [7:0] in_1,
  output out_2,
  output out_3,
  output out_4,
  output out_5
);

  wire a_larger, A_out, and_1_out, and_2_out, and_3_out, and_4_out, and_5_out, and_6_out, and_7_out,
       and_8_out, and_16_out, and_17_out, and_18_out, and_19_out, and_20_out, and_21_out, and_22_out,
       and_23_out, and_24_out, and_25_out, and_26_out, and_27_out, and_28_out, and_29_out, and_30_out,
       and_31_out, and_32_out, and_33_out, and_34_out, and_35_out, and_36_out, and_37_out, and_38_out,
       and_39_out, and_40_out, and_41_out, and_42_out, and_43_out, c_out, C_out_2, clk_1_clk_e, clk_1_clk_s,
       clk_1_main, decoder_1_out0, decoder_1_out1, decoder_1_out2, decoder_1_out3, decoder_2_out0,
       decoder_2_out1, decoder_2_out2, decoder_2_out3, decoder_3_out0, decoder_3_out1, decoder_3_out2,
       decoder_3_out3, decoder_3_out4, decoder_3_out5, decoder_3_out6, decoder_3_out7, decoder_4_out0,
       decoder_4_out1, decoder_4_out2, decoder_4_out3, E_out, enable_ACC, enable_BUS_1, enable_IN_OUT,
       enable_R0, enable_R1, enable_R2, enable_R3, equal, led, not_1_out, not_2_out, not_3_out, or_5_out,
       or_6_out, or_7_out, or_8_out, or_10_out, or_11_out, or_12_out, or_13_out, or_14_out, or_15_out,
       or_16_out, set_FLAG, set_IN_OUT, set_MAR, set_R0, set_R1, set_R2, set_R3, set_RAM, set_TMP,
       stepper_1_step1, stepper_1_step2, stepper_1_step3, stepper_1_step4, stepper_1_step5, stepper_1_step6,
       Z_out, zero;
  wire [2:0] to_ULA;

  or or_1 (enable_R0, and_1_out, and_5_out);
  or or_2 (enable_R1, and_2_out, and_6_out);
  or or_3 (enable_R2, and_3_out, and_7_out);
  or or_4 (enable_R3, and_4_out, and_8_out);
  and and_1 (and_1_out, decoder_1_out0, clk_1_clk_e, or_5_out);
  and and_2 (and_2_out, decoder_1_out1, clk_1_clk_e, or_5_out);
  and and_3 (and_3_out, decoder_1_out2, clk_1_clk_e, or_5_out);
  and and_4 (and_4_out, decoder_1_out3, clk_1_clk_e, or_5_out);
  and and_5 (and_5_out, decoder_2_out0, clk_1_clk_e, or_6_out);
  and and_6 (and_6_out, decoder_2_out1, clk_1_clk_e, or_6_out);
  and and_7 (and_7_out, decoder_2_out2, clk_1_clk_e, or_6_out);
  and and_8 (and_8_out, decoder_2_out3, clk_1_clk_e, or_6_out);
  Clk clk_1 (.clk_s(clk_1_clk_s), .main(clk_1_main), .clk_e(clk_1_clk_e));
  and and_9 (out_4, clk_1_clk_e, or_7_out);
  and and_10 (out_4, clk_1_clk_e, or_10_out);
  and and_11 (enable_ACC, clk_1_clk_e, or_8_out);
  and and_12 (enable_IN_OUT, clk_1_clk_e, and_40_out);
  and and_13 (to_ULA[0], stepper_1_step5, in_1[0], in_1[3]);
  and and_14 (to_ULA[1], stepper_1_step5, in_1[0], in_1[2]);
  and and_15 (to_ULA[2], stepper_1_step5, in_1[0], in_1[1]);
  or or_5 (or_5_out, and_24_out, and_36_out, and_28_out, and_32_out);
  or or_6 (or_6_out, and_26_out, and_25_out, and_34_out);
  Decoder #(.enable("false"), .select(2)) decoder_1 (
    .out0(decoder_1_out0), .out1(decoder_1_out1), .out2(decoder_1_out2), .out3(decoder_1_out3),
    .sel({in_1[6], in_1[7]}));
  Decoder #(.enable("false"), .select(2)) decoder_2 (
    .out0(decoder_2_out0), .out1(decoder_2_out1), .out2(decoder_2_out2), .out3(decoder_2_out3),
    .sel(in_1[5:4]));
  or or_7 (or_7_out, stepper_1_step1, and_27_out, and_29_out, and_27_out);
  or or_8 (or_8_out, stepper_1_step3, and_39_out, and_42_out, and_41_out);
  or or_9 (enable_BUS_1, stepper_1_step1, and_31_out, and_30_out, and_27_out);
  or or_10 (or_10_out, stepper_1_step2, and_43_out, and_38_out, and_37_out, and_35_out);
  not not_1 (not_1_out, in_1[0]);
  Decoder #(.enable("false"), .select(3)) decoder_3 (
    .out0(decoder_3_out0), .out1(decoder_3_out1), .out2(decoder_3_out2), .out3(decoder_3_out3),
    .out4(decoder_3_out4), .out5(decoder_3_out5), .out6(decoder_3_out6), .out7(decoder_3_out7),
    .sel(in_1[3:1]));
  and and_16 (and_16_out, not_1_out, decoder_3_out0);
  and and_17 (and_17_out, not_1_out, decoder_3_out1);
  and and_18 (and_18_out, not_1_out, decoder_3_out2);
  and and_19 (and_19_out, not_1_out, decoder_3_out3);
  and and_20 (and_20_out, not_1_out, decoder_3_out4);
  and and_21 (and_21_out, not_1_out, decoder_3_out5);
  and and_22 (and_22_out, not_1_out, decoder_3_out6);
  and and_23 (and_23_out, not_1_out, decoder_3_out7);
  and C (C_out_2, c_out, in_1[4]);
  and A (A_out, a_larger, in_1[5]);
  and E (E_out, equal, in_1[6]);
  and Z (Z_out, zero, in_1[7]);
  and and_24 (and_24_out, stepper_1_step4, not_1_out);
  and and_25 (and_25_out, stepper_1_step4, and_16_out);
  and and_26 (and_26_out, stepper_1_step4, and_17_out);
  and and_27 (and_27_out, stepper_1_step4, and_18_out);
  and and_28 (and_28_out, stepper_1_step4, and_19_out);
  and and_29 (and_29_out, stepper_1_step4, and_20_out);
  and and_30 (and_30_out, stepper_1_step4, and_21_out);
  and and_31 (and_31_out, stepper_1_step4, and_22_out);
  and and_32 (and_32_out, stepper_1_step4, and_23_out, in_1[4]);
  not not_2 (not_2_out, in_1[4]);
  or or_11 (or_11_out, C_out_2, A_out, E_out, Z_out);
  and and_33 (and_33_out, in_1[3], in_1[2], in_1[1]);
  Stepper stepper_1 (
    .in_1(clk_1_main), .step1(stepper_1_step1), .step2(stepper_1_step2), .step3(stepper_1_step3),
    .step4(stepper_1_step4), .step5(stepper_1_step5), .step6(stepper_1_step6), .out_2(led));
  and and_34 (and_34_out, stepper_1_step5, in_1[0]);
  and and_35 (and_35_out, stepper_1_step5, and_16_out);
  and and_36 (and_36_out, stepper_1_step5, and_17_out);
  and and_37 (and_37_out, stepper_1_step5, and_18_out);
  and and_38 (and_38_out, stepper_1_step5, and_20_out);
  and and_39 (and_39_out, stepper_1_step5, and_21_out);
  and and_40 (and_40_out, and_32_out, stepper_1_step5, not_2_out);
  not not_3 (not_3_out, and_33_out);
  and and_41 (and_41_out, stepper_1_step6, not_3_out, in_1[0]);
  and and_42 (and_42_out, stepper_1_step6, and_18_out);
  and and_43 (and_43_out, stepper_1_step6, and_29_out, or_11_out);
  or or_12 (or_12_out, stepper_1_step1, and_27_out, and_30_out, and_25_out, and_26_out, and_29_out);
  or or_13 (or_13_out, stepper_1_step3, and_28_out, and_38_out, and_39_out, and_42_out, and_43_out);
  or or_14 (or_14_out, stepper_1_step1, and_27_out, and_30_out, and_41_out);
  Decoder #(.enable("false"), .select(2)) decoder_4 (
    .out0(decoder_4_out0), .out1(decoder_4_out1), .out2(decoder_4_out2), .out3(decoder_4_out3),
    .sel(in_1[7:6]));
  or or_15 (or_15_out, and_35_out, and_41_out, and_37_out, and_40_out);
  or or_16 (or_16_out, and_34_out, and_31_out);
  and and_44 (out_5, clk_1_clk_s, stepper_1_step2);
  and and_45 (set_MAR, clk_1_clk_s, or_12_out);
  and and_46 (out_3, clk_1_clk_s, or_13_out);
  and and_47 (out_2, clk_1_clk_s, or_14_out);
  and and_48 (set_TMP, clk_1_clk_s, and_24_out);
  and and_49 (set_RAM, clk_1_clk_s, and_36_out);
  and and_50 (set_FLAG, clk_1_clk_s, or_16_out);
  and and_51 (set_IN_OUT, clk_1_clk_s, and_32_out);
  and and_52 (set_R0, clk_1_clk_s, or_15_out, decoder_4_out0);
  and and_53 (set_R1, clk_1_clk_s, or_15_out, decoder_4_out1);
  and and_54 (set_R2, clk_1_clk_s, or_15_out, decoder_4_out2);
  and and_55 (set_R3, clk_1_clk_s, or_15_out, decoder_4_out3);

  // Other names for the same wires on the sheet: IR[7:0] = in_1; enable_IAR = out_4; input_output = in_1[4];
  //   data_address = in_1[5]; set_ACC = out_2; set_IAR = out_3; set_IR = out_5
endmodule

module bus_1 (
  input  [7:0] in_1,
  input  in_2,
  output [7:0] out_3
);

  Multiplexer #(.width(8)) multiplexer_1 (.in0(in_1), .in1(8'h1), .out(out_3), .sel(in_2));
endmodule

module flag (
  input  in_1,
  input  in_2,
  input  in_3,
  input  in_4,
  input  in_5,
  output out_6,
  output out_7,
  output out_8,
  output out_9
);

  Register #(.width(4)) register_1 (
    .D({in_4, in_3, in_2, in_1}), .Q({out_9, out_8, out_7, out_6}), .clk(in_5));  // open: en, clr
endmodule
