// Logisim project kaike_maciel_8bits.circ as structural Verilog: 14 circuits, main circuit somador_1bit
module main (
  input  in_1
);

  wire flags_out_6, flags_out_7, flags_out_8, flags_out_9, or_1_out, uc_1_out_30, ula_1_a_igual_b,
       ula_1_a_maior_b, ula_1_c_out, ula_1_igual_0, undriven_2, undriven_3, undriven_4, undriven_5,
       undriven_6, undriven_7, undriven_8, undriven_9, undriven_10, undriven_11, undriven_12, undriven_13,
       undriven_14, undriven_15, undriven_16, undriven_17, undriven_18, undriven_19;
  wire [2:0] undriven;
  wire [7:0] bus1_out_3, controlled_buffer_1_out, IAR_q, IR_q, R0_q, R1_q, R2_q, R3_q, ram_1_dout,
       register_1_q, register_2_q, register_3_q, ula_1_saida;

  ULA ula_1 (
    .A(controlled_buffer_1_out), .B(bus1_out_3), .SAIDA(ula_1_saida), .in_1(undriven), .c_out(ula_1_c_out),
    .igual_0(ula_1_igual_0), .a_maior_b(ula_1_a_maior_b), .a_igual_b(ula_1_a_igual_b));
  Register register_1 (.D(controlled_buffer_1_out), .Q(register_1_q), .clk(undriven_3));  // open: en, clr
  bus_1 bus1 (.in_1(register_1_q), .out_3(bus1_out_3), .in_2(uc_1_out_30));
  Register register_2 (.D(ula_1_saida), .Q(register_2_q), .clk(undriven_2));  // open: en, clr
  flag flags (
    .in_1(ula_1_c_out), .in_2(ula_1_igual_0), .in_3(ula_1_a_maior_b), .in_4(ula_1_a_igual_b),
    .in_5(undriven_5), .out_6(flags_out_6), .out_7(flags_out_7), .out_8(flags_out_8), .out_9(flags_out_9));
  assign controlled_buffer_1_out = undriven_6 ? R0_q : 8'bz;  // Controlled_Buffer controlled_buffer_1
  Register R0 (.D(controlled_buffer_1_out), .Q(R0_q), .clk(undriven_4));  // open: en, clr
  assign controlled_buffer_1_out = undriven_9 ? register_2_q : 8'bz;  // Controlled_Buffer controlled_buffer_2
  assign controlled_buffer_1_out = undriven_8 ? R1_q : 8'bz;  // Controlled_Buffer controlled_buffer_3
  Register R1 (.D(controlled_buffer_1_out), .Q(R1_q), .clk(undriven_7));  // open: en, clr
  assign controlled_buffer_1_out = undriven_13 ? R2_q : 8'bz;  // Controlled_Buffer controlled_buffer_4
  Register R2 (.D(controlled_buffer_1_out), .Q(R2_q), .clk(undriven_12));  // open: en, clr
  Register IAR (.D(controlled_buffer_1_out), .Q(IAR_q), .clk(undriven_11));  // open: en, clr
  assign controlled_buffer_1_out = undriven_10 ? IAR_q : 8'bz;  // Controlled_Buffer controlled_buffer_5
  UC uc_1 (
    .ula(undriven), .c_out(flags_out_6), .larger(flags_out_7), .equal(flags_out_8), .zero(flags_out_9),
    .flag_s(undriven_5), .out_30(uc_1_out_30), .tmp(undriven_3), .r0_S(undriven_4), .r0_e(undriven_6),
    .r1_s(undriven_7), .r1_e(undriven_8), .r2_s(undriven_12), .r2_e(undriven_13), .r3_s(undriven_15),
    .r3_e(undriven_16), .mar_s(undriven_17), .acc_e(undriven_9), .acc_s(undriven_2), .iar_s(undriven_11),
    .iar_e(undriven_10), .ir(IR_q), .ram_s(undriven_18), .ram_e(undriven_19), .init(undriven_14));  // open: ir_s, in_out, data_addr, io_e, io_s
  LED led_1 (.in(undriven_14));
  Register IR (.D(controlled_buffer_1_out), .Q(IR_q));  // open: en, clk, clr
  Register R3 (.D(controlled_buffer_1_out), .Q(R3_q), .clk(undriven_15));  // open: en, clr
  assign controlled_buffer_1_out = undriven_16 ? R3_q : 8'bz;  // Controlled_Buffer controlled_buffer_6
  or or_1 (or_1_out, undriven_18, undriven_19);
  Register register_3 (.D(controlled_buffer_1_out), .Q(register_3_q), .clk(undriven_17));  // open: en, clr
  RAM ram_1 (
    .addr(register_3_q), .we(undriven_18), .oe(undriven_19), .clk(or_1_out), .din(controlled_buffer_1_out),
    .dout(ram_1_dout));
  assign controlled_buffer_1_out = undriven_19 ? ram_1_dout : 8'bz;  // Controlled_Buffer controlled_buffer_7
endmodule

module somador_1bit (
  input  c_in,
  input  in_2,
  input  in_3,
  output out_4,
  output c_out
);

  wire and_1_out, and_2_out, and_3_out, xor_1_out;

  xor xor_1 (xor_1_out, in_2, in_3);
  and and_1 (and_1_out, in_2, c_in);
  and and_2 (and_2_out, in_2, in_3);
  and and_3 (and_3_out, in_3, c_in);
  xor xor_2 (out_4, xor_1_out, c_in);
  or or_1 (c_out, and_1_out, and_2_out, and_3_out);
endmodule

module somador_8bit (
  input  in_1,
  input  [7:0] in_2,
  input  [7:0] in_3,
  output [7:0] out_4,
  output out_5
);

  wire somador_1bit_1_c_out, somador_1bit_2_c_out, somador_1bit_3_c_out, somador_1bit_4_c_out,
       somador_1bit_5_c_out, somador_1bit_6_c_out, somador_1bit_7_c_out;

  somador_1bit somador_1bit_1 (
    .in_2(in_2[0]), .in_3(in_2[0]), .c_in(in_1), .c_out(somador_1bit_1_c_out), .out_4(out_4[0]));
  somador_1bit somador_1bit_2 (
    .in_2(in_2[1]), .in_3(in_3[1]), .c_in(somador_1bit_1_c_out), .c_out(somador_1bit_2_c_out),
    .out_4(out_4[1]));
  somador_1bit somador_1bit_3 (
    .in_2(in_2[2]), .in_3(in_3[2]), .c_in(somador_1bit_2_c_out), .c_out(somador_1bit_3_c_out),
    .out_4(out_4[2]));
  somador_1bit somador_1bit_4 (
    .in_2(in_2[3]), .in_3(in_3[3]), .c_in(somador_1bit_3_c_out), .c_out(somador_1bit_4_c_out),
    .out_4(out_4[3]));
  somador_1bit somador_1bit_5 (
    .in_2(in_2[4]), .in_3(in_3[4]), .c_in(somador_1bit_4_c_out), .c_out(somador_1bit_5_c_out),
    .out_4(out_4[4]));
  somador_1bit somador_1bit_6 (
    .in_2(in_2[5]), .in_3(in_3[5]), .c_in(somador_1bit_5_c_out), .c_out(somador_1bit_6_c_out),
    .out_4(out_4[5]));
  somador_1bit somador_1bit_7 (
    .in_2(in_2[6]), .in_3(in_3[6]), .c_in(somador_1bit_6_c_out), .c_out(somador_1bit_7_c_out),
    .out_4(out_4[6]));
  somador_1bit somador_1bit_8 (
    .in_2(in_2[7]), .in_3(in_3[7]), .c_in(somador_1bit_7_c_out), .c_out(out_5), .out_4(out_4[7]));

  assign in_3[0] = in_2[0];
endmodule

module memoria_1bit (
  input  in_1,
  input  in_2,
  output out_3
);

  wire nand_1_out, nand_2_out, nand_4_out;

  nand nand_1 (nand_1_out, in_1, in_2);
  nand nand_2 (nand_2_out, nand_1_out, in_2);
  // Probe on nand_1_out
  nand nand_3 (out_3, nand_1_out, nand_4_out);
  nand nand_4 (nand_4_out, out_3, nand_2_out);
endmodule

module registrador (
  input  [7:0] in_1,
  input  in_2,
  input  in_3,
  output [7:0] out_4
);

  wire memoria_1bit_1_out_3, memoria_1bit_2_out_3, memoria_1bit_3_out_3, memoria_1bit_4_out_3,
       memoria_1bit_5_out_3, memoria_1bit_6_out_3, memoria_1bit_7_out_3, memoria_1bit_8_out_3;

  memoria_1bit memoria_1bit_1 (.in_1(in_1[0]), .in_2(in_2), .out_3(memoria_1bit_1_out_3));
  memoria_1bit memoria_1bit_2 (.in_1(in_1[1]), .in_2(in_2), .out_3(memoria_1bit_2_out_3));
  memoria_1bit memoria_1bit_3 (.in_1(in_1[2]), .in_2(in_2), .out_3(memoria_1bit_3_out_3));
  memoria_1bit memoria_1bit_4 (.in_1(in_1[3]), .in_2(in_2), .out_3(memoria_1bit_4_out_3));
  memoria_1bit memoria_1bit_5 (.in_1(in_1[4]), .in_2(in_2), .out_3(memoria_1bit_5_out_3));
  memoria_1bit memoria_1bit_6 (.in_1(in_1[5]), .in_2(in_2), .out_3(memoria_1bit_6_out_3));
  memoria_1bit memoria_1bit_7 (.in_1(in_1[6]), .in_2(in_2), .out_3(memoria_1bit_7_out_3));
  memoria_1bit memoria_1bit_8 (.in_1(in_1[7]), .in_2(in_2), .out_3(memoria_1bit_8_out_3));
  and and_1 (out_4[0], memoria_1bit_1_out_3, in_3);
  and and_2 (out_4[1], memoria_1bit_2_out_3, in_3);
  and and_3 (out_4[2], memoria_1bit_3_out_3, in_3);
  and and_4 (out_4[3], memoria_1bit_4_out_3, in_3);
  and and_5 (out_4[4], memoria_1bit_5_out_3, in_3);
  and and_6 (out_4[5], memoria_1bit_6_out_3, in_3);
  and and_7 (out_4[6], memoria_1bit_7_out_3, in_3);
  and and_8 (out_4[7], memoria_1bit_8_out_3, in_3);
endmodule

module memoria (
);

  Register register_1 ();  // open: D, en, Q, clk, clr
endmodule

module shift_left (
  input  c_in,
  input  [7:0] in_2,
  output [7:0] out_3,
  output c_out
);


  assign c_out = in_2[7];
  assign out_3 = {in_2[6:0], c_in};
endmodule

module shift_right (
  input  c_in,
  input  [7:0] in_2,
  output [7:0] out_3,
  output c_out
);


  assign c_out = in_2[0];
  assign out_3 = {c_in, in_2[7:1]};
endmodule

module ULA (
  input  [2:0] in_1,
  input  [7:0] A,
  input  [7:0] B,
  output c_out,
  output [7:0] SAIDA,
  output igual_0,
  output a_maior_b,
  output a_igual_b
);

  wire adder_1_cout, left_c_out, or_2_out, right_c_out;
  wire [7:0] adder_1_out, and_1_out, left_out_3, not_1_out, or_1_out, right_out_3, xor_1_out;

  Adder adder_1 (.a(A), .b(B), .out(adder_1_out), .cin(1'b0), .cout(adder_1_cout));
  shift_right right (.in_2(A), .c_in(1'b0), .c_out(right_c_out), .out_3(right_out_3));
  shift_left left (.in_2(A), .c_in(1'b0), .c_out(left_c_out), .out_3(left_out_3));
  assign not_1_out = ~A;  // NOT_Gate not_1, 8 bits wide
  assign and_1_out = A & B;  // AND_Gate and_1, 8 bits wide
  assign or_1_out = A | B;  // OR_Gate or_1, 8 bits wide
  assign xor_1_out = A ^ B;  // XOR_Gate xor_1, 8 bits wide
  Comparator comparator_1 (.a(A), .b(B), .gt(a_maior_b), .eq(a_igual_b));  // open: lt
  Multiplexer #(.select(3), .width(8)) multiplexer_1 (
    .in0(adder_1_out), .in1(right_out_3), .in2(left_out_3), .in3(not_1_out), .in4(and_1_out), .in5(or_1_out),
    .in6(xor_1_out), .in7(A), .out(SAIDA), .sel(in_1));
  Multiplexer #(.select(3)) multiplexer_2 (
    .in0(adder_1_cout), .in1(right_c_out), .in2(left_c_out), .in3(1'b0), .in4(1'b0), .in5(1'b0), .in6(1'b0),
    .in7(1'b0), .out(c_out), .sel(in_1));
  or or_2 (or_2_out, SAIDA[0], SAIDA[1], SAIDA[2], SAIDA[3], SAIDA[4], SAIDA[5], SAIDA[6], SAIDA[7]);
  not not_2 (igual_0, or_2_out);
endmodule

module clk (
  output clk_set,
  output out_2,
  output clk_enable
);

  wire clk_d_out;

  Clock #(.highDuration(2), .lowDuration(2), .phaseOffset(2)) main_clk (.out(out_2));
  Clock #(.highDuration(2), .lowDuration(2), .phaseOffset(3)) clk_d (.out(clk_d_out));
  and and_1 (clk_set, clk_d_out, out_2);
  or or_1 (clk_enable, out_2, clk_d_out);
endmodule

module stepper (
  input  in_1,
  output out_2,
  output out_3,
  output out_4,
  output out_5,
  output out_6,
  output out_7,
  output out_8
);

  wire decoder_1_out7;
  wire [2:0] counter_1_q;

  Counter #(.max('h7), .width(3)) counter_1 (
    .D(counter_1_q), .Q(counter_1_q), .clk(in_1), .clr(decoder_1_out7));  // open: load, count, carry, up
  Decoder #(.enable("false"), .select(3)) decoder_1 (
    .out0(out_2), .out1(out_3), .out2(out_4), .out3(out_5), .out4(out_6), .out5(out_7), .out6(out_8),
    .out7(decoder_1_out7), .sel(counter_1_q));
endmodule

module UC (
  input  r0_S,
  input  r0_e,
  input  r1_s,
  input  r1_e,
  input  r2_s,
  input  r2_e,
  input  r3_s,
  input  r3_e,
  input  mar_s,
  input  tmp,
  input  ram_s,
  input  [2:0] ula,
  input  c_out,
  input  ram_e,
  input  larger,
  input  init,
  input  equal,
  input  zero,
  input  flag_s,
  input  [7:0] ir,
  input  acc_e,
  input  acc_s,
  input  iar_s,
  input  iar_e,
  input  ir_s,
  input  in_out,
  input  data_addr,
  input  io_e,
  input  io_s,
  output out_30
);

  wire and_5_out, and_6_out, and_7_out, and_8_out, and_9_out, and_10_out, and_11_out, and_12_out, and_16_out,
       and_17_out, and_18_out, and_19_out, and_20_out, and_21_out, and_22_out, and_23_out, and_24_out,
       and_25_out, and_26_out, and_27_out, and_28_out, and_29_out, and_30_out, and_31_out, and_32_out,
       and_33_out, and_34_out, and_35_out, and_36_out, and_37_out, and_39_out, and_40_out, and_41_out,
       and_42_out, and_43_out, and_44_out, and_45_out, and_46_out, and_47_out, clk_enable, clk_set,
       clock_out_2, decoder_1_out0, decoder_1_out1, decoder_1_out2, decoder_1_out3, decoder_2_out0,
       decoder_2_out1, decoder_2_out2, decoder_2_out3, decoder_3_out0, decoder_3_out1, decoder_3_out2,
       decoder_3_out3, decoder_3_out4, decoder_3_out5, decoder_3_out6, decoder_3_out7, decoder_4_out0,
       decoder_4_out1, decoder_4_out2, decoder_4_out3, not_1_out, not_2_out, not_3_out, or_5_out, or_7_out,
       or_8_out, or_9_out, or_10_out, or_11_out, or_12_out, or_13_out, or_14_out, or_15_out, or_16_out, S1,
       S2, S3, S4, S5, S6;

  or or_1 (r0_e, and_5_out, and_9_out);
  or or_2 (r1_e, and_6_out, and_10_out);
  or or_3 (r2_e, and_7_out, and_11_out);
  or or_4 (r3_e, and_8_out, and_12_out);
  clk clock (.clk_set(clk_set), .out_2(clock_out_2), .clk_enable(clk_enable));
  and and_1 (iar_e, clk_enable, or_5_out);
  and and_2 (ram_e, clk_enable, or_7_out);
  and and_3 (acc_e, clk_enable, or_8_out);
  and and_4 (io_e, clk_enable, and_44_out);
  and and_5 (and_5_out, clk_enable, or_9_out, decoder_2_out0);
  and and_6 (and_6_out, clk_enable, or_9_out, decoder_2_out1);
  and and_7 (and_7_out, clk_enable, or_9_out, decoder_2_out2);
  and and_8 (and_8_out, clk_enable, or_9_out, decoder_2_out3);
  and and_9 (and_9_out, clk_enable, or_10_out, decoder_1_out0);
  and and_10 (and_10_out, clk_enable, or_10_out, decoder_1_out1);
  and and_11 (and_11_out, clk_enable, or_10_out, decoder_1_out2);
  and and_12 (and_12_out, clk_enable, or_10_out, decoder_1_out3);
  or or_5 (or_5_out, S1, and_32_out, and_34_out, and_35_out);
  and and_13 (ula[0], S5, ir[0], ir[0]);
  and and_14 (ula[1], S5, ir[0], ir[1]);
  and and_15 (ula[2], S5, ir[0], ir[2]);
  or or_6 (out_30, S1, and_36_out, and_35_out, and_32_out);
  or or_7 (or_7_out, S2, and_47_out, and_42_out, and_41_out, and_39_out);
  or or_8 (or_8_out, S3, and_43_out, and_46_out, and_45_out);
  or or_9 (or_9_out, and_29_out, and_40_out, and_33_out, and_37_out);
  or or_10 (or_10_out, and_31_out, and_30_out, and_34_out);
  Decoder #(.enable("false"), .select(2)) decoder_1 (
    .out0(decoder_1_out0), .out1(decoder_1_out1), .out2(decoder_1_out2), .out3(decoder_1_out3),
    .sel({data_addr, in_out}));
  Decoder #(.enable("false"), .select(2)) decoder_2 (
    .out0(decoder_2_out0), .out1(decoder_2_out1), .out2(decoder_2_out2), .out3(decoder_2_out3),
    .sel({ir[6], ir[7]}));
  stepper stepper_1 (
    .in_1(clock_out_2), .out_3(S1), .out_4(S2), .out_5(S3), .out_6(S4), .out_7(S5), .out_8(S6), .out_2(init));
  not not_1 (not_1_out, ir[0]);
  Decoder #(.enable("false"), .select(3)) decoder_3 (
    .out0(decoder_3_out0), .out1(decoder_3_out1), .out2(decoder_3_out2), .out3(decoder_3_out3),
    .out4(decoder_3_out4), .out5(decoder_3_out5), .out6(decoder_3_out6), .out7(decoder_3_out7),
    .sel({ir[1], ir[2], ir[3]}));
  and and_16 (and_16_out, not_1_out, decoder_3_out0);
  and and_17 (and_17_out, not_1_out, decoder_3_out1);
  and and_18 (and_18_out, not_1_out, decoder_3_out2);
  and and_19 (and_19_out, not_1_out, decoder_3_out3);
  and and_20 (and_20_out, not_1_out, decoder_3_out4);
  and and_21 (and_21_out, not_1_out, decoder_3_out5);
  and and_22 (and_22_out, not_1_out, decoder_3_out6);
  and and_23 (and_23_out, not_1_out, decoder_3_out7);
  and and_24 (and_24_out, ir[4], c_out);
  and and_25 (and_25_out, data_addr, larger);
  and and_26 (and_26_out, ir[6], equal);
  and and_27 (and_27_out, ir[7], zero);
  and and_28 (and_28_out, ir[0], ir[1], ir[2]);
  not not_2 (not_2_out, and_28_out);
  and and_29 (and_29_out, S4, ir[0]);
  and and_30 (and_30_out, S4, and_16_out);
  and and_31 (and_31_out, S4, and_17_out);
  and and_32 (and_32_out, S4, and_18_out);
  and and_33 (and_33_out, S4, and_19_out);
  and and_34 (and_34_out, S4, and_20_out);
  and and_35 (and_35_out, S4, and_21_out);
  and and_36 (and_36_out, S4, and_22_out);
  and and_37 (and_37_out, S4, and_23_out, ir[4]);
  not not_3 (not_3_out, ir[4]);
  and and_38 (and_34_out, S5, ir[0]);
  and and_39 (and_39_out, S5, and_16_out);
  and and_40 (and_40_out, S5, and_17_out);
  and and_41 (and_41_out, S5, and_18_out);
  and and_42 (and_42_out, S5, and_20_out);
  and and_43 (and_43_out, S5, and_21_out);
  and and_44 (and_44_out, S5, and_23_out, not_3_out);
  or or_11 (or_11_out, and_24_out, and_25_out, and_26_out, and_27_out);
  and and_45 (and_45_out, S6, ir[0], not_2_out);
  and and_46 (and_46_out, S6, and_18_out);
  and and_47 (and_47_out, S6, and_21_out, or_11_out);
  or or_12 (or_12_out, S1, and_32_out, and_35_out, and_30_out, and_31_out, and_34_out);
  or or_13 (or_13_out, S3, and_33_out, and_42_out, and_43_out, and_46_out, and_47_out);
  or or_14 (or_14_out, and_29_out, and_32_out, and_35_out, and_34_out);
  or or_15 (or_15_out, and_36_out, and_34_out);
  or or_16 (or_16_out, and_39_out, and_45_out, and_41_out, and_44_out);
  Decoder #(.enable("false"), .select(2)) decoder_4 (
    .out0(decoder_4_out0), .out1(decoder_4_out1), .out2(decoder_4_out2), .out3(decoder_4_out3),
    .sel({ir[6], ir[7]}));
  and and_48 (ir_s, clk_set, S2);
  and and_49 (mar_s, clk_set, or_12_out);
  and and_50 (iar_s, clk_set, or_13_out);
  and and_51 (acc_s, clk_set, or_14_out);
  and and_52 (ram_s, clk_set, and_40_out);
  and and_53 (tmp, clk_set, and_29_out);
  and and_54 (flag_s, clk_set, or_15_out);
  and and_55 (io_s, clk_set, and_37_out);
  and and_56 (r0_S, clk_set, or_16_out, decoder_4_out0);
  and and_57 (r1_s, clk_set, or_16_out, decoder_4_out1);
  and and_58 (r2_s, clk_set, or_16_out, decoder_4_out2);
  and and_59 (r3_s, clk_set, or_16_out, decoder_4_out3);

  assign ir[5] = data_addr;

  // Other names for the same wires on the sheet: input_output = in_out; ACC_enable = acc_e; ACC_set = acc_s;
  //   bus1 = out_30; FLAGS_set = flag_s; IAR_enable = iar_e; IAR_set = iar_s; IO_enable = io_e; IO_set = io_s;
  //   data_adress = data_addr; IR_set = ir_s; MAR_set = mar_s; R0_enable = r0_e; R0_set = r0_S; R1_enable = r1_e;
  //   R1_set = r1_s; R2_enable = r2_e; R2_set = r2_s; R3_enable = r3_e; R3_set = r3_s; RAM_enable = ram_e;
  //   RAM_set = ram_s; TMP_set = tmp
endmodule

module bus_1 (
  input  [7:0] in_1,
  input  in_2,
  output [7:0] out_3
);

  Multiplexer #(.width(8)) multiplexer_1 (.in0(in_1), .in1(8'h1), .out(out_3), .sel(in_2));
endmodule

module flag (
  input  in_1,
  input  in_2,
  input  in_3,
  input  in_4,
  input  in_5,
  output out_6,
  output out_7,
  output out_8,
  output out_9
);

  Register #(.width(4)) register_1 (
    .D({in_4, in_3, in_2, in_1}), .Q({out_9, out_8, out_7, out_6}), .clk(in_5));  // open: en, clr
endmodule
